# Fritzing sketch ButtonInput_schematic (saved by Fritzing 0.9.2b)
breadboards: 1

parts:
  R1 = Resistor [tolerance=±5% resistance=10k package=THT]
  Part1 = Arduino Uno (Rev3)
  S1 = Pushbutton [package="[SMD]"]

nets:
  N1: R1.Pin_0, Part1.GND
  N2: R1.Pin_1, Part1.D7, S1.Pin_3, S1.Pin_4
  N3: Part1.5V, S1.Pin_1, S1.Pin_2
