# Fritzing sketch PotentiometerInput (saved by Fritzing 0.9.2b)
breadboards: 1

parts:
  Part2 = Arduino Uno (Rev3) - ICSP
  R3 = Rotary Potentiometer (Large) [maximum_resistance=100kΩ package=THT]

nets:
  N1: Part2.A1, R3.wiper
  N2: Part2.5V, R3.leg1
  N3: Part2.GND, R3.leg2
