# Fritzing sketch Audio_LineIn_Input (saved by Fritzing 0.9.2b)
breadboards: 1

parts:
  BAT1 = BC9VPC [package=bc9vpc]
  BAT2 = BC9VPC [package=bc9vpc]
  U4 = 3.5mm Audio Jack [package=audio-jack-3.5mm-smd]
  TL082 = ADTL082 - Dual JFET Input Op Amps [part_number=ADTL082]
  TL082_1 = AnalogDevices_ADTL082ARZ_subpart1 [part_number=ADTL082]  # not connected
  R2 = Rotary Potentiometer (Large) [maximum_resistance=10kΩ package=THT]
  R5 = Resistor [tolerance=±5% resistance=100k package="0603 [SMD]"]
  R6 = Resistor [tolerance=±5% resistance=100k package="0603 [SMD]"]
  C2_4_7nF = Capacitor [package=cap-pth-small2]
  C1 = Electrolytic Capacitor [capacitance=10µF package="1010 [SMD, electrolytic]"]
  Part1 = Arduino Uno (Rev3)
  R4 = Resistor [tolerance=±5% resistance=100k package="0603 [SMD]"]

nets:
  N1: BAT1.V+, TL082.connector8
  N2: BAT1.V-, BAT2.V+, U4.SLEEVE, R2.leg2
  N3: BAT2.V-, TL082.connector4
  N4: U4.RIGHT, TL082.connector3
  N5: TL082.connector1, C1.-, R4.Pin_0
  N6: TL082.connector2, R2.wiper, R4.Pin_1
  N7: R5.Pin_0, C2_4_7nF.2, Part1.GND
  N8: R5.Pin_1, R6.Pin_0, C2_4_7nF.1, C1.+, Part1.A0
  N9: R6.Pin_1, Part1.5V
