# Fritzing sketch HIFI_Output (saved by Fritzing 0.9.2b)
breadboards: 1

parts:
  R11_3_9KΩ1 = Resistor [tolerance=±0.5% resistance=220 package="0402 [SMD]"]
  C9_4_7nF1 = Ceramic Capacitor [capacitance="100 nF" package="1206 [SMD, multilayer]"]
  R14 = Resistor [tolerance=±5% resistance=1M package="0402 [SMD]"]
  R15 = Resistor [tolerance=±1% resistance=1M package="0402 [SMD]"]
  JACK_Out1 = 3.5mm Audio Jack [package=audio-jack-3.5mm-smd]
  Part1 = Arduino Uno (Rev3)

nets:
  N1: R11_3_9KΩ1.Pin_0, Part1.D9_PWM
  N2: R11_3_9KΩ1.Pin_1, C9_4_7nF1.1, R14.Pin_1, R15.Pin_1, JACK_Out1.LEFT
  N3: C9_4_7nF1.0, JACK_Out1.SLEEVE, Part1.GND
  N4: R14.Pin_0, R15.Pin_0, Part1.D10_PWM/SS
