# Fritzing sketch MIDI_DIN-Socket_Input (saved by Fritzing 0.9.2b)
circuit board: 3.95015cm x 1.83734cm
breadboards: 1

parts:
  220Ω = Resistor [tolerance=±5% resistance=220 package="0603 [SMD]"]
  MIDI_Input = DIN-5 jack (MIDI) [package=THT]
  optocoupler = IC, DIP package, 8 pins [chip_label=6N138]
  220Ω_2 = Resistor [tolerance=±5% resistance=220 package="0603 [SMD]"]
  part = Resistor [tolerance=±5% resistance=220 package="0603 [SMD]"]  # not connected
  4_7K = Resistor [tolerance=±5% resistance=4.7k package=THT]
  diode = Rectifier Diode [part_number=1N4001 package="300 mil [THT]"]
  Arduino_Mega = Arduino Mega 2560 (Rev3)

nets:
  N1: 220Ω.Pin_0, optocoupler.pin2, diode.cathode
  N2: 220Ω.Pin_1, MIDI_Input.4
  N3: MIDI_Input.5, optocoupler.pin3, diode.anode
  N4: optocoupler.pin5, 4_7K.Pin_0, Arduino_Mega.GND
  N5: optocoupler.pin6, 220Ω_2.Pin_0, Arduino_Mega.D0_RX0
  N6: optocoupler.pin7, 4_7K.Pin_1
  N7: optocoupler.pin8, 220Ω_2.Pin_1
