# Fritzing sketch MIDI_DIN-Socket_Output (saved by Fritzing 0.9.2b)

parts:
  Arduino = Arduino Uno (Rev3)
  R1 = Resistor [tolerance=±5% resistance=220 package=THT]
  R2 = Resistor [tolerance=±5% resistance=220 package=THT]
  MIDI_Socket = DIN-5 jack (MIDI) [package=THT]

nets:
  N1: Arduino.GND, MIDI_Socket.2
  N2: Arduino.D1/TX, R1.Pin_1
  N3: Arduino.5V, R2.Pin_0
  N4: R1.Pin_0, MIDI_Socket.5
  N5: R2.Pin_1, MIDI_Socket.4
